# Fritzing sketch CoMeter++ (saved by Fritzing 0.9.3b)
circuit board: 10cm x 8cm
breadboards: 3

parts:
  Bauteil1 = Arduino Nano (Rev3.0)
  U1 = TMA0515D
  D2 = Rectifier Diode [part_number=1N4001 package="300 mil [THT]"]
  D3 = Rectifier Diode [part_number=1N4001 package="300 mil [THT]"]
  Bauteil2 = Adafruit ADS1115 16Bit I2C ADC [part_number="Adafruit #1085"]
  D4 = Rectifier Diode [part_number=1N4001 package="300 mil [THT]"]
  D5 = Rectifier Diode [part_number=1N4001 package="300 mil [THT]"]
  U2 = INA121 [package="DIP (Dual Inline) [THT]"]
  U3 = OP07 [package="DIP (Dual Inline) [THT]"]
  R4 = Resistor [tolerance=±5% resistance=10 package=THT]
  R5 = Resistor [tolerance=±20% resistance=10k package=THT]
  R6 = Resistor [tolerance=±5% resistance=47k package=THT]
  U4 = LM78xx [package=to-92]
  R7 = Resistor [tolerance=±5% resistance=47k package=THT]
  R8 = Resistor [tolerance=±2% resistance=1k package=THT]
  R9 = Resistor [tolerance=±2% resistance=1k package=THT]
  C1 = Tantalum Capacitor [capacitance=1μF package="100 mil [THT, tantalum]"]
  U5 = OP07 [package="DIP (Dual Inline) [THT]"]
  U6 = OP07 [package="DIP (Dual Inline) [THT]"]
  R13 = Resistor [tolerance=±5% resistance=22k package=THT]
  R14 = Resistor [tolerance=±5% resistance=47k package=THT]
  R15 = Resistor [tolerance=±5% resistance=10k package=THT]
  R17 = Resistor [tolerance=±5% resistance=22k package=THT]
  R18 = Resistor [tolerance=±5% resistance=47k package=THT]
  R19 = Resistor [tolerance=±5% resistance=10k package=THT]
  Bauteil3 = Adafruit MCP4725 Breakout Board - 12-Bit DAC [part_number="Adafruit #935"]
  D6 = Rectifier Diode [part_number=1N4001 package="300 mil [THT]"]
  D7 = Rectifier Diode [part_number=1N4001 package="300 mil [THT]"]
  D8 = Rectifier Diode [part_number=1N4001 package="300 mil [THT]"]
  D9 = Rectifier Diode [part_number=1N4001 package="300 mil [THT]"]
  R20 = Resistor [tolerance=±5% resistance=1k package=THT]
  R21 = Resistor [tolerance=±5% resistance=1k package=THT]
  R22 = Resistor [tolerance=±5% resistance=1k package=THT]
  R23 = Resistor [tolerance=±5% resistance=1k package=THT]
  J3 = female pin header, 4 pins [form="♀ (female)"]
  J4 = female pin header, 15 pins [form="♀ (female)"]
  R24 = Resistor [tolerance=±2% resistance=1k package=THT]
  R25 = Resistor [tolerance=±2% resistance=1k package=THT]
  D10 = Rectifier Diode [part_number=1N4001 package="300 mil [THT]"]
  D11 = Rectifier Diode [part_number=1N4001 package="300 mil [THT]"]
  J6 = female pin header, 3 pins [form="♀ (female)"]
  R26 = 1 Ω 5 W resistor [package=THT]
  J1 = female pin header, 3 pins [form="♀ (female)"]
  J7 = female pin header, 3 pins [form="♀ (female)"]
  J8 = female pin header, 2 pins [form="♀ (female)"]
  J9 = female pin header, 2 pins [form="♀ (female)"]
  R28 = Resistor [tolerance=±5% resistance=1k package=THT]
  J10 = female pin header, 2 pins [form="♀ (female)"]
  J11 = female pin header, 2 pins [form="♀ (female)"]
  J12 = female pin header, 4 pins [form="♀ (female)"]
  U9 = LM78xx [package=to-92]
  R32 = Resistor [tolerance=±5% resistance=1k package=THT]
  U10 = OP07 [package="DIP (Dual Inline) [THT]"]
  R33 = Resistor [tolerance=±5% resistance=22k package=THT]
  R34 = Resistor [tolerance=±5% resistance=10k package=THT]
  R35 = Resistor [tolerance=±5% resistance=47k package=THT]

nets:
  N1: Bauteil1.D1/TX, J4.pin1
  N2: Bauteil1.D0/RX, J4.pin2
  N3: Bauteil1.RESET, J4.pin3
  GND: Bauteil1.GND, U1.VIN-, U1.COM, D2.anode, D3.anode, Bauteil2.ADDR, Bauteil2.GND, D4.anode, D5.anode, U2.REF, R5.Pin_1, U4.GND, U5.+IN, U6.+IN, Bauteil3.GND, D6.anode, D7.anode, D8.anode, D9.anode, J4.pin4, D10.anode, D11.anode, J9.pin2, J10.pin1, J11.pin1, J12.pin2, U9.OUT, U10.+IN
  N4: Bauteil1.D2, J4.pin5
  N5: Bauteil1.D3, J4.pin6
  N6: Bauteil1.D4, J4.pin7
  N7: Bauteil1.D5, J4.pin8
  N8: Bauteil1.D6, J4.pin9
  N9: Bauteil1.D7, J4.pin10
  N10: Bauteil1.D8, J4.pin11
  N11: Bauteil1.D9, J4.pin12
  N12: Bauteil1.D10, J4.pin13
  N13: Bauteil1.D11/MOSI, J4.pin14
  N14: Bauteil1.D12/MISO, J4.pin15
  VDD: Bauteil1.5V, U1.VIN+, Bauteil2.VDD, Bauteil3.VDD, J12.pin4
  N15: Bauteil1.A7, D6.cathode, R32.Pin_0
  N16: Bauteil1.A6, D2.cathode, R28.Pin_0
  N17: Bauteil1.A5, Bauteil2.SCL, Bauteil3.SCL
  N18: Bauteil1.A4, Bauteil2.SDA, Bauteil3.SDA
  N19: Bauteil1.A3, D8.cathode, R23.Pin_0
  N20: Bauteil1.A2, D7.cathode, R22.Pin_0
  N21: Bauteil1.A1, D3.cathode, R21.Pin_0
  N22: Bauteil1.A0, D9.cathode, R20.Pin_0
  N23: U1.VOUT-, U2.V-, U3.V-, U5.V-, U6.V-, J12.pin3, U9.GND, U10.V-
  N24: U1.VOUT+, U2.V+, U3.V+, U4.IN, U5.V+, U6.V+, J12.pin1, U10.V+
  N25: Bauteil2.AIN3, R25.Pin_0, D11.cathode
  N26: Bauteil2.AIN2, R24.Pin_0, D10.cathode
  N27: Bauteil2.AIN1, D5.cathode, R9.Pin_0
  N28: Bauteil2.AIN0, D4.cathode, R8.Pin_0
  N29: U2.RG#0, J8.pin1
  N30: U2.-IN, R26.Pin_0, J1.pin2
  N31: U2.+IN, J7.pin2
  N32: U2.OUT, R6.Pin_1
  N33: U2.RG#7, J8.pin2
  N34: U3.-IN, R4.Pin_0, R6.Pin_0
  N35: U3.+IN, R5.Pin_0, R7.Pin_1
  N36: U3.OUT, R4.Pin_1, R25.Pin_1
  N37: U4.OUT, R7.Pin_0
  N38: R8.Pin_1, J6.pin3
  N39: R9.Pin_1, J6.pin2
  N40: C1.-, R26.Pin_1, J7.pin3
  N41: C1.+, J1.pin1
  N42: U5.-IN, R13.Pin_1, R14.Pin_1, R15.Pin_0
  N43: U5.OUT, R15.Pin_1, R28.Pin_1
  N44: U6.-IN, R17.Pin_1, R18.Pin_0, R19.Pin_1
  N45: U6.OUT, R18.Pin_1, J9.pin1
  N46: R13.Pin_0, R17.Pin_0, U9.IN, R33.Pin_0
  N47: R14.Pin_0, J10.pin2
  N48: R19.Pin_0, Bauteil3.VOUT
  N49: R20.Pin_1, J3.pin4
  N50: R21.Pin_1, J3.pin3
  N51: R22.Pin_1, J3.pin2
  N52: R23.Pin_1, J3.pin1
  N53: R24.Pin_1, J6.pin1
  N54: J1.pin3, J7.pin1
  N55: J11.pin2, R35.Pin_0
  N56: R32.Pin_1, U10.OUT, R34.Pin_1
  N57: U10.-IN, R33.Pin_1, R34.Pin_0, R35.Pin_1

notes:
  Conrad Wolf
  Hochschule Coburg
  CoMeter v1

custom parts:
  TMA0515D: DC/DC converter TMA0515D
  Adafruit ADS1115 16Bit I2C ADC: For microcontrollers without an analog-to-digital converter or when you want a higher-precision ADC, the ADS1115 provides 16-bit precision at 860 samples/second over I2C. The chip can be configured as 4 single-ended input channels, or two differential channels. As a nice bonus, it even includes a programmable gain amplifier, up to x16, to help boost up smaller single/differential signals to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
  INA121: Instrumentation amplifier INA121
  OP07: OP07 operational amplifier
  LM78xx: Voltage Regulator LM78xx 5V.
  Adafruit MCP4725 Breakout Board - 12-Bit DAC: Your microcontroller probably has an ADC (analog -> digital converter) but does it have a DAC (digital -> analog converter)??? Now it can! This breakout board features the easy-to-use MCP4725 12-bit DAC. Control it via I2C and send it the value you want it to output, and the VOUT pin will have it. Great for audio / analog projects, such as when you can't use PWM but need a sine wave or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
  1 Ω 5 W resistor: 1 Ω 5 W power resistor
